# Fritzing sketch RX (saved by Fritzing 0.9.3b)

parts:
  nRF24L01_PA1 = nRF24L01 power adapter [package="DIP (Dual Inline) [THT]"]
  Часть2 = Arduino Nano (Rev3.0)
  Q1 = MOSFET-NCHANNEL [package=to220v]
  R1 = Resistor [tolerance=±5% resistance=100 package="1206 [SMD]"]
  Q2 = MOSFET-NCHANNEL [package=to220v]
  Q3 = MOSFET-NCHANNEL [package=to220v]
  Q4 = MOSFET-NCHANNEL [package=to220v]
  Q5 = MOSFET-NCHANNEL [package=to220v]
  R2 = Resistor [tolerance=±5% resistance=100 package="1206 [SMD]"]
  R3 = Resistor [tolerance=±5% resistance=100 package="1206 [SMD]"]
  R4 = Resistor [tolerance=±5% resistance=100 package="1206 [SMD]"]
  R5 = Resistor [tolerance=±5% resistance=100 package="1206 [SMD]"]
  Q6 = MOSFET-NCHANNEL [package=to220v]
  Q9 = MOSFET-NCHANNEL [package=to220v]
  Q10 = MOSFET-NCHANNEL [package=to220v]
  Q11 = MOSFET-NCHANNEL [package=to220v]
  Q12 = MOSFET-NCHANNEL [package=to220v]
  R6 = Resistor [tolerance=±5% resistance=100 package="1206 [SMD]"]
  R7 = Resistor [tolerance=±5% resistance=100 package="1206 [SMD]"]
  R8 = Resistor [tolerance=±5% resistance=100 package="1206 [SMD]"]
  R9 = Resistor [tolerance=±5% resistance=100 package="1206 [SMD]"]
  R10 = Resistor [tolerance=±5% resistance=100 package="1206 [SMD]"]
  J1 = Basic Servo
  R11 = Resistor [tolerance=±5% resistance=100 package="1206 [SMD]"]
  Q13 = MOSFET-NCHANNEL [package=to220v]
  Q14 = MOSFET-NCHANNEL [package=to220v]
  R12 = Resistor [tolerance=±5% resistance=100 package="1206 [SMD]"]
  J2 = Basic Servo
  IC1 = DC-DC 5V step-up [chip_label="DC-DC 5V step-up" package="DIP (Dual Inline) [THT]"]
  18650_holder1 = 18650 holder [package="DIP (Dual Inline) [THT]"]

nets:
  GND: nRF24L01_PA1.GND, Часть2.GND, J2.gnd, IC1.GND
  VCC: nRF24L01_PA1.VCC, Часть2.5V, J2.vcc, IC1.5V
  N1: nRF24L01_PA1.CE, Часть2.D9
  N2: nRF24L01_PA1.CSN, Часть2.D10
  N3: nRF24L01_PA1.SCK, Часть2.D13/SCK
  N4: nRF24L01_PA1.MO, Часть2.D11/MOSI
  N5: nRF24L01_PA1.MI, Часть2.D12/MISO
  N6: Часть2.D1/TX, J1.pulse
  N7: Часть2.D0/RX, J2.pulse
  N8: Часть2.D3, R12.Pin_1
  N9: Часть2.D4, R7.Pin_1
  N10: Часть2.D5, R10.Pin_1
  N11: Часть2.D6, R9.Pin_1
  N12: Часть2.D7, R8.Pin_1
  N13: Часть2.D8, R6.Pin_1
  N14: Часть2.A5, R11.Pin_0
  N15: Часть2.A4, R5.Pin_0
  N16: Часть2.A3, R4.Pin_0
  N17: Часть2.A2, R3.Pin_0
  N18: Часть2.A1, R2.Pin_0
  N19: Часть2.A0, R1.Pin_0
  N20: Q1.G, R1.Pin_1
  N21: Q2.G, R2.Pin_1
  N22: Q3.G, R3.Pin_1
  N23: Q4.G, R4.Pin_1
  N24: Q5.G, R5.Pin_1
  N25: Q5.S, Q12.S, Q14.S, IC1.IN-, 18650_holder1.holder_-
  N26: Q6.G, R6.Pin_0
  N27: Q9.G, R8.Pin_0
  N28: Q10.G, R9.Pin_0
  N29: Q11.G, R10.Pin_0
  N30: Q12.G, R7.Pin_0
  N31: R11.Pin_1, Q13.G
  N32: Q14.G, R12.Pin_0
  N33: IC1.IN+, 18650_holder1.holder_+

notes:
  FPV камера

custom parts:
  nRF24L01 power adapter: Адаптер для питания nRF
  DC-DC 5V step-up: Повышающий модуль постоянного напряжения
  18650 holder: Акум формата 18650 в холдере
